# Fritzing sketch WiringSchema (saved by Fritzing 0.9.0b)
breadboards: 1

parts:
  Onderdeel1 = EasyDriver_v44
  U1 = ESP8266 WiFi Module [part_number=ESP8266]
  REG1 = LD33 Low-Dropout Voltage Regulator
  Onderdeel2 = Arduino Nano (Rev3.0)
  Onderdeel3 = EasyDriver_v44
  M3 = Stepper Motor - Bipolar
  M4 = Stepper Motor - Bipolar
  Power_plug1 = Power plug

nets:
  GND: Onderdeel1.GND, U1.GND, REG1.GND, Onderdeel2.GND, Onderdeel3.GND, Power_plug1.GND
  N1: Onderdeel1.V+, Onderdeel3.V+, Power_plug1.VCC
  N2: Onderdeel1.STEP, Onderdeel2.D7
  N3: Onderdeel1.DIR, Onderdeel2.D6
  N4: Onderdeel1.OUT2A, M4.A
  N5: Onderdeel1.OUT2B, M4.C
  N6: Onderdeel1.OUT1A, M4.B
  N7: Onderdeel1.OUT1B, M4.D
  N8: U1.RXD, Onderdeel2.D0/RX
  N9: U1.VCC, U1.RST, REG1.Vout
  N10: U1.TXD, Onderdeel2.D1/TX
  VIN: REG1.Vin, Onderdeel2.5V
  N11: Onderdeel2.D8, Onderdeel3.DIR
  N12: Onderdeel2.D9, Onderdeel3.STEP
  N13: Onderdeel3.OUT2A, M3.A
  N14: Onderdeel3.OUT2B, M3.C
  N15: Onderdeel3.OUT1A, M3.B
  N16: Onderdeel3.OUT1B, M3.D

custom parts:
  ESP8266 WiFi Module: Generic WiFi Module based on the ESP8266 with onboard PCB antenna and UART communications
